# Fritzing sketch Front Panel (saved by Fritzing 0.9.3b)
breadboards: 1

parts:
  Start_Button = IC, DIP package, 6 pins [chip_label=IC]
  Pause_Button = IC, DIP package, 6 pins [chip_label=IC]
  Stop_Button = IC, DIP package, 6 pins [chip_label=IC]

nets:
  Start Light +: Start_Button.pin1
  Start Button -: Start_Button.pin2
  Button Panel -: Start_Button.pin3, Start_Button.pin6, Pause_Button.pin3, Pause_Button.pin6, Stop_Button.pin3, Stop_Button.pin6
  Button Panel +: Start_Button.pin4, Pause_Button.pin4, Stop_Button.pin4
  Pause Light +: Pause_Button.pin1
  Pause Button -: Pause_Button.pin2
  Stop Light +: Stop_Button.pin1
  Stop Button -: Stop_Button.pin2
