# Fritzing sketch PLC_Diag_1 (saved by Fritzing 0.9.3b)
breadboards: 1

parts:
  IC1 = IC, DIP package, 64 pins [chip_label="Micro 850" part_number=2080-L50E-48QBB]
  IC2 = IC, DIP package, 8 pins [chip_label="Power Supply" part_number=2080-PS-120-240VAC]
  IC9 = IC, DIP package, 8 pins [chip_label="DPDT Relay" part_number=52111]
  IC4 = IC, DIP package, 8 pins [chip_label="DPDT Relay" part_number=52111]
  IC6 = IC, DIP package, 8 pins [chip_label="DPDT Relay" part_number=52111]
  IC8 = IC, DIP package, 8 pins [chip_label="DPDT Relay" part_number=52111]
  D1 = Diode [package=diode-1n4148]
  D2 = Diode [package=diode-1n4148]
  D3 = Diode [package=diode-1n4148]
  D4 = Diode [package=diode-1n4148]
  J3 = Camdenboss CTB0158-9 [part_number=CTB0158-9 package=THT]  # not connected
  J5 = Camdenboss CTB0158-11 [part_number=CTB0158-11 package=THT]  # not connected
  J6 = Camdenboss CTB0158-12 [part_number=CTB0158-12 package=THT]
  J8 = Camdenboss CTB0158-12 [part_number=CTB0158-12 package=THT]
  D5 = Diode [package=diode-1n4148]
  D6 = Diode [package=diode-1n4148]
  D7 = Diode [package=diode-1n4148]
  J9 = Camdenboss CTB0158-12 [package=THT]
  D8 = Diode [package=diode-1n4148]
  D9 = Diode [package=diode-1n4148]
  D10 = Diode [package=diode-1n4148]
  D11 = Diode [package=diode-1n4148]
  D12 = Diode [package=diode-1n4148]
  D13 = Diode [package=diode-1n4148]
  D14 = Diode [package=diode-1n4148]

nets:
  N1: IC1.pin1, IC2.pin1
  N2: IC1.pin2, IC2.pin3
  N3: IC1.pin3, IC1.pin9, IC1.pin17, IC2.pin2, IC6.pin7, IC8.pin2
  N4: IC1.pin4, IC9.pin1, D4.C
  N5: IC1.pin5, IC4.pin5
  N6: IC1.pin6, IC6.pin1, D2.C
  N7: IC1.pin7, J8.pin9, D7.C
  N8: IC1.pin8, IC1.pin16, IC1.pin24, IC1.pin64, IC2.pin4, IC6.pin5, IC8.pin4, IC8.pin8, D3.A, J8.pin4, J8.pin6, J8.pin10, J8.pin12, D5.A, D6.A, D7.A, J9.pin2, J9.pin4, J9.pin6, J9.pin8, J9.pin10, J9.pin12, D8.A, D9.A, D10.A, D11.A, D12.A, D13.A, D14.A
  N9: IC1.pin10, J8.pin11, D8.C
  N10: IC1.pin11, J9.pin1, D9.C
  N11: IC1.pin12, J9.pin3, D10.C
  N12: IC1.pin13, J9.pin5, D11.C
  N13: IC1.pin14, J9.pin7, D12.C
  N14: IC1.pin15, J9.pin9, D13.C
  N15: IC1.pin18, J9.pin11, D14.C
  N16: IC2.pin6, J6.pin10
  N17: IC2.pin7, J6.pin11
  N18: IC2.pin8, J6.pin12
  N19: IC9.pin6, IC4.pin3, J8.pin1
  N20: IC9.pin7, IC4.pin2, J8.pin2
  N21: IC9.pin8, D4.A
  N22: IC4.pin1, D1.C
  N23: IC4.pin6, IC6.pin4
  N24: IC4.pin8, D1.A
  N25: IC6.pin3, IC8.pin1, D3.C
  N26: IC6.pin6, J8.pin3, D5.C
  N27: IC6.pin8, D2.A
  N28: IC8.pin3, J8.pin5, D6.C
  N29: IC8.pin6, J8.pin7
  N30: IC8.pin7, J8.pin8
  Earth: J6.terminal_10
  Neutral: J6.terminal_11
  Hot: J6.terminal_12
  Waste Pump Relay Out: J8.terminal_1
  Waste Pump Relay In: J8.terminal_2
  Air Solenoid +: J8.terminal_3
  Air Solenoid -: J8.terminal_4
  Main Water Solenoid +: J8.terminal_5
  Main Water Solenoid -: J8.terminal_6
  Pressure Washer Relay Out: J8.terminal_7
  Pressure Washer Relay In: J8.terminal_8
  Solenoid 1-1 +: J8.terminal_9
  Solenoid 1-1 -: J8.terminal_10
  Solenoid 1-2 +: J8.terminal_11
  Solenoid 1-2 -: J8.terminal_12
  Solenoid 1-3 +: J9.terminal_1
  Solenoid 1-3 -: J9.terminal_2
  Solenoid 1-4 +: J9.terminal_3
  Solenoid 1-4 -: J9.terminal_4
  Solenoid 2-1 +: J9.terminal_5
  Solenoid 2-1 -: J9.terminal_6
  Solenoid 2-2 +: J9.terminal_7
  Solenoid 2-2 -: J9.terminal_8
  Solenoid 2-3 +: J9.terminal_9
  Solenoid 2-3 -: J9.terminal_10
  Solenoid 2-4 +: J9.terminal_11
  Solenoid 2-4 -: J9.terminal_12
