# Fritzing sketch PLC_Diag_2 - Copy (saved by Fritzing 0.9.3b)
breadboards: 1

parts:
  IC1 = IC, DIP package, 8 pins [chip_label="Power Supply" part_number=2080-PS-120-240VAC]
  Waste_Pump_PLC_Relay = IC, DIP package, 8 pins [chip_label="DPDT Relay" part_number=52111]
  Waste_Pump_Level_Switch_Relay = IC, DIP package, 8 pins [chip_label="DPDT Relay" part_number=52111]
  Air_Valve_Control_Relay = IC, DIP package, 8 pins [chip_label="DPDT Relay" part_number=52111]
  Main_Water_Control_Relay = IC, DIP package, 8 pins [chip_label="DPDT Relay" part_number=52111]
  D1 = Diode [package=diode-1n4148]
  D2 = Diode [package=diode-1n4148]
  D3 = Diode [package=diode-1n4148]
  D4 = Diode [package=diode-1n4148]
  J4 = Camdenboss CTB0158-12 [package=THT]
  J6 = Camdenboss CTB0158-12 [package=THT]
  J7 = Camdenboss CTB0158-12 [package=THT]
  IC2 = IC, DIP package, 64 pins [chip_label="Micro 850" part_number=2080-L50E-48QBB]
  J8 = Camdenboss CTB0158-2 [package=THT]
  Main_Air_Valve_Relay = IC, DIP package, 8 pins [chip_label="DPDT Relay" part_number=52111]
  Main_Water_Valve_Relay = IC, DIP package, 8 pins [chip_label="DPDT Relay" part_number=52111]
  D15 = Diode [package=diode-1n4148]
  D16 = Diode [package=diode-1n4148]
  Valve_2-4_Relay = IC, DIP package, 8 pins [chip_label="DPDT Relay" part_number=52111]
  Valve_2-3_Relay = IC, DIP package, 8 pins [chip_label="DPDT Relay" part_number=52111]
  D17 = Diode [package=diode-1n4148]
  D18 = Diode [package=diode-1n4148]
  Valve_1-3_Relay = IC, DIP package, 8 pins [chip_label="DPDT Relay" part_number=52111]
  D19 = Diode [package=diode-1n4148]
  Valve_1-2_Relay = IC, DIP package, 8 pins [chip_label="DPDT Relay" part_number=52111]
  D20 = Diode [package=diode-1n4148]
  Valve_1-1_Relay = IC, DIP package, 8 pins [chip_label="DPDT Relay" part_number=52111]
  D21 = Diode [package=diode-1n4148]
  Valve_1-4_Relay = IC, DIP package, 8 pins [chip_label="DPDT Relay" part_number=52111]
  Valve_2-1_Relay = IC, DIP package, 8 pins [chip_label="DPDT Relay" part_number=52111]
  Valve_2-2_Relay = IC, DIP package, 8 pins [chip_label="DPDT Relay" part_number=52111]
  D22 = Diode [package=diode-1n4148]
  D23 = Diode [package=diode-1n4148]
  D24 = Diode [package=diode-1n4148]
  J5 = Camdenboss CTB0158-4 [part_number=CTB0158-4 package=THT]
  J9 = Camdenboss CTB0158-12 [part_number=CTB0158-12 package=THT]
  J10 = Camdenboss CTB0158-12 [part_number=CTB0158-12 package=THT]

nets:
  N1: IC1.pin1, IC2.pin1
  N2: IC1.pin2, Waste_Pump_PLC_Relay.pin7, Waste_Pump_Level_Switch_Relay.pin2, Air_Valve_Control_Relay.pin7, Main_Water_Control_Relay.pin2, Main_Water_Control_Relay.pin7, J4.pin2, J4.pin4, J4.pin6, J4.pin8, IC2.pin3, IC2.pin9, IC2.pin17, IC2.pin25
  N3: IC1.pin3, IC2.pin2
  N4: IC1.pin4, Waste_Pump_PLC_Relay.pin8, Waste_Pump_Level_Switch_Relay.pin7, Waste_Pump_Level_Switch_Relay.pin8, Air_Valve_Control_Relay.pin2, Air_Valve_Control_Relay.pin5, Air_Valve_Control_Relay.pin8, Main_Water_Control_Relay.pin4, Main_Water_Control_Relay.pin5, Main_Water_Control_Relay.pin8, D1.A, D2.A, D3.A, D4.A, IC2.pin8, IC2.pin16, IC2.pin24, IC2.pin30, IC2.pin41, IC2.pin50, IC2.pin57, IC2.pin64, Main_Water_Valve_Relay.pin8, D15.A, Valve_2-4_Relay.pin8, Valve_2-3_Relay.pin8, D17.A, D18.A, Valve_1-3_Relay.pin8, D19.A, Valve_1-2_Relay.pin8, D20.A, Valve_1-1_Relay.pin8, D21.A, Valve_1-4_Relay.pin8, Valve_2-1_Relay.pin8, Valve_2-2_Relay.pin8, D22.A, D23.A, D24.A
  N5: IC1.pin6, J4.pin10
  N6: IC1.pin7, J4.pin11
  N7: IC1.pin8, J4.pin12
  N8: Waste_Pump_PLC_Relay.pin1, D4.C, IC2.pin4
  NC: Waste_Pump_PLC_Relay.pin2, Waste_Pump_PLC_Relay.pin3, Waste_Pump_PLC_Relay.pin4, J4.terminal_1
  N9: Waste_Pump_PLC_Relay.pin6, Waste_Pump_Level_Switch_Relay.pin3, J9.pin1
  N10: Waste_Pump_Level_Switch_Relay.pin1, D1.C, J4.pin9, IC2.pin62, IC2.pin63
  N11: Waste_Pump_Level_Switch_Relay.pin5, IC2.pin5
  N12: Waste_Pump_Level_Switch_Relay.pin6, Air_Valve_Control_Relay.pin4
  N13: Air_Valve_Control_Relay.pin1, D2.C, IC2.pin6
  N14: Air_Valve_Control_Relay.pin3, Main_Water_Control_Relay.pin1, D3.C
  N15: Air_Valve_Control_Relay.pin6, Main_Air_Valve_Relay.pin1, D16.C
  N16: Main_Water_Control_Relay.pin3, Main_Water_Valve_Relay.pin1, D15.C
  N17: Main_Water_Control_Relay.pin6, J9.pin2
  N18: J4.pin3, IC2.pin59
  N19: J4.pin5, IC2.pin60
  N20: J4.pin7, IC2.pin61
  Stop Button +: J4.terminal_2
  Stop Button -: J4.terminal_3
  Pause Button +: J4.terminal_4
  Pause Button -: J4.terminal_5
  Start Button +: J4.terminal_6
  Start Button -: J4.terminal_7
  Level Switch +: J4.terminal_8
  Level Switch -: J4.terminal_9
  Earth: J4.terminal_10
  Neutral: J4.terminal_11
  Hot: J4.terminal_12
  Solenoid 1-3 +: J6.terminal_1
  Solenoid 1-3 -: J6.terminal_2
  Solenoid 1-4 +: J6.terminal_3
  Solenoid 1-4 -: J6.terminal_4
  Solenoid 2-1 +: J6.terminal_5
  Solenoid 2-1 -: J6.terminal_6
  Solenoid 2-2 +: J6.terminal_7
  Solenoid 2-2 -: J6.terminal_8
  Solenoid 2-3 +: J6.terminal_9
  Solenoid 2-3 -: J6.terminal_10
  Solenoid 2-4 +: J6.terminal_11
  Solenoid 2-4 -: J6.terminal_12
  Stop Light +: J7.terminal_1
  Stop Light -: J7.terminal_2
  Pause Light +: J7.terminal_3
  Pause Light -: J7.terminal_4
  Start Light +: J7.terminal_5
  Start Light -: J7.terminal_6
  Error Light +: J7.terminal_7
  Error Light -: J7.terminal_8
  Washing Indicator +: J7.terminal_9
  Washing Indicator -: J7.terminal_10
  Drying Indicator +: J7.terminal_11
  Drying Indicator -: J7.terminal_12
  N21: IC2.pin7, Valve_1-1_Relay.pin1, D21.C
  N22: IC2.pin10, Valve_1-2_Relay.pin1, D20.C
  N23: IC2.pin11, Valve_1-3_Relay.pin1, D19.C
  N24: IC2.pin12, Valve_1-4_Relay.pin1, D24.C
  N25: IC2.pin13, Valve_2-1_Relay.pin1, D22.C
  N26: IC2.pin14, Valve_2-2_Relay.pin1, D23.C
  N27: IC2.pin15, Valve_2-3_Relay.pin1, D18.C
  N28: IC2.pin18, Valve_2-4_Relay.pin1, D17.C
  Pumping Indicator +: J8.terminal_1
  Pumping Indicator -: J8.terminal_2
  N29: Main_Air_Valve_Relay.pin2, Main_Air_Valve_Relay.pin5, Main_Water_Valve_Relay.pin2, Main_Water_Valve_Relay.pin5, Valve_1-3_Relay.pin2, Valve_1-3_Relay.pin5, Valve_1-2_Relay.pin2, Valve_1-2_Relay.pin5, Valve_1-1_Relay.pin2, Valve_1-1_Relay.pin5, J5.pin1
  N30: Main_Air_Valve_Relay.pin3, J9.pin9
  N31: Main_Air_Valve_Relay.pin4, Main_Air_Valve_Relay.pin7, Main_Water_Valve_Relay.pin4, Main_Water_Valve_Relay.pin7, Valve_1-3_Relay.pin4, Valve_1-3_Relay.pin7, Valve_1-2_Relay.pin4, Valve_1-2_Relay.pin7, Valve_1-1_Relay.pin4, Valve_1-1_Relay.pin7, J5.pin2
  N32: Main_Air_Valve_Relay.pin6, J9.pin10
  N33: Main_Air_Valve_Relay.pin8, D16.A
  N34: Main_Water_Valve_Relay.pin3, J9.pin11
  N35: Main_Water_Valve_Relay.pin6, J9.pin12
  N36: Valve_2-4_Relay.pin2, Valve_2-4_Relay.pin5, Valve_2-3_Relay.pin2, Valve_2-3_Relay.pin5, Valve_1-4_Relay.pin2, Valve_1-4_Relay.pin5, Valve_2-1_Relay.pin2, Valve_2-1_Relay.pin5, Valve_2-2_Relay.pin2, Valve_2-2_Relay.pin5, J5.pin3
  N37: Valve_2-4_Relay.pin3, J10.pin9
  N38: Valve_2-4_Relay.pin4, Valve_2-4_Relay.pin7, Valve_2-3_Relay.pin4, Valve_2-3_Relay.pin7, Valve_1-4_Relay.pin4, Valve_1-4_Relay.pin7, Valve_2-1_Relay.pin4, Valve_2-1_Relay.pin7, Valve_2-2_Relay.pin4, Valve_2-2_Relay.pin7, J5.pin4
  N39: Valve_2-4_Relay.pin6, J10.pin10
  N40: Valve_2-3_Relay.pin3, J10.pin7
  N41: Valve_2-3_Relay.pin6, J10.pin8
  N42: Valve_1-3_Relay.pin3, J9.pin7
  N43: Valve_1-3_Relay.pin6, J9.pin8
  N44: Valve_1-2_Relay.pin3, J9.pin5
  N45: Valve_1-2_Relay.pin6, J9.pin6
  N46: Valve_1-1_Relay.pin3, J9.pin3
  N47: Valve_1-1_Relay.pin6, J9.pin4
  N48: Valve_1-4_Relay.pin3, J10.pin1
  N49: Valve_1-4_Relay.pin6, J10.pin2
  N50: Valve_2-1_Relay.pin3, J10.pin3
  N51: Valve_2-1_Relay.pin6, J10.pin4
  N52: Valve_2-2_Relay.pin3, J10.pin5
  N53: Valve_2-2_Relay.pin6, J10.pin6
