# Fritzing sketch PLC_Diag_2 (saved by Fritzing 0.9.3b)
breadboards: 1

parts:
  Waste_Pump_PLC_Relay = IC, DIP package, 8 pins [chip_label="DPDT Relay" part_number=52111]
  Waste_Pump_Level_Switch_Relay = IC, DIP package, 8 pins [chip_label="DPDT Relay" part_number=52111]
  Man_Air_Valve_PLC_Relay = IC, DIP package, 8 pins [chip_label="DPDT Relay" part_number=52111]
  Pressure_Washer_PLC_Relay = IC, DIP package, 8 pins [chip_label="DPDT Relay" part_number=52111]
  D1 = Diode [package=diode-1n4148]
  D2 = Diode [package=diode-1n4148]
  D3 = Diode [package=diode-1n4148]
  D4 = Diode [package=diode-1n4148]
  Allen_Bradley_Micro_850 = IC, DIP package, 64 pins [chip_label="Micro 850" part_number=2080-L50E-48QBB]
  Main_Air_Valve_Relay = IC, DIP package, 8 pins [chip_label="DPDT Relay" part_number=52111]
  Main_Water_Valve_Relay = IC, DIP package, 8 pins [chip_label="DPDT Relay" part_number=52111]
  D15 = Diode [package=diode-1n4148]
  D16 = Diode [package=diode-1n4148]
  Valve_2-4_Relay = IC, DIP package, 8 pins [chip_label="DPDT Relay" part_number=52111]
  Valve_2-3_Relay = IC, DIP package, 8 pins [chip_label="DPDT Relay" part_number=52111]
  D17 = Diode [package=diode-1n4148]
  D18 = Diode [package=diode-1n4148]
  Valve_1-3_Relay = IC, DIP package, 8 pins [chip_label="DPDT Relay" part_number=52111]
  D19 = Diode [package=diode-1n4148]
  Valve_1-2_Relay = IC, DIP package, 8 pins [chip_label="DPDT Relay" part_number=52111]
  D20 = Diode [package=diode-1n4148]
  Valve_1-1_Relay = IC, DIP package, 8 pins [chip_label="DPDT Relay" part_number=52111]
  D21 = Diode [package=diode-1n4148]
  Valve_1-4_Relay = IC, DIP package, 8 pins [chip_label="DPDT Relay" part_number=52111]
  Valve_2-1_Relay = IC, DIP package, 8 pins [chip_label="DPDT Relay" part_number=52111]
  Valve_2-2_Relay = IC, DIP package, 8 pins [chip_label="DPDT Relay" part_number=52111]
  D22 = Diode [package=diode-1n4148]
  D23 = Diode [package=diode-1n4148]
  D24 = Diode [package=diode-1n4148]

nets:
  N1: Waste_Pump_PLC_Relay.pin1, D4.C, Allen_Bradley_Micro_850.pin4
  NC: Waste_Pump_PLC_Relay.pin2, Waste_Pump_PLC_Relay.pin3, Waste_Pump_PLC_Relay.pin4, Waste_Pump_PLC_Relay.pin5, Waste_Pump_Level_Switch_Relay.pin4
  Waste Pump Contactor +: Waste_Pump_PLC_Relay.pin6, Waste_Pump_Level_Switch_Relay.pin3
  PLC PSU C2 +24: Waste_Pump_PLC_Relay.pin7, Waste_Pump_Level_Switch_Relay.pin2, Man_Air_Valve_PLC_Relay.pin7, Pressure_Washer_PLC_Relay.pin2, Pressure_Washer_PLC_Relay.pin7, Allen_Bradley_Micro_850.pin3, Allen_Bradley_Micro_850.pin9, Allen_Bradley_Micro_850.pin17, Allen_Bradley_Micro_850.pin25
  PLC PSU C2 -24: Waste_Pump_PLC_Relay.pin8, Waste_Pump_Level_Switch_Relay.pin7, Waste_Pump_Level_Switch_Relay.pin8, Man_Air_Valve_PLC_Relay.pin2, Man_Air_Valve_PLC_Relay.pin5, Man_Air_Valve_PLC_Relay.pin8, Pressure_Washer_PLC_Relay.pin4, Pressure_Washer_PLC_Relay.pin5, Pressure_Washer_PLC_Relay.pin8, D1.A, D2.A, D3.A, D4.A, Allen_Bradley_Micro_850.pin8, Allen_Bradley_Micro_850.pin16, Allen_Bradley_Micro_850.pin24, Allen_Bradley_Micro_850.pin30, Allen_Bradley_Micro_850.pin41, Allen_Bradley_Micro_850.pin50, Allen_Bradley_Micro_850.pin57, Allen_Bradley_Micro_850.pin64, Main_Water_Valve_Relay.pin8, D15.A, Valve_2-4_Relay.pin8, Valve_2-3_Relay.pin8, D17.A, D18.A, Valve_1-3_Relay.pin8, D19.A, Valve_1-2_Relay.pin8, D20.A, Valve_1-1_Relay.pin8, D21.A, Valve_1-4_Relay.pin8, Valve_2-1_Relay.pin8, Valve_2-2_Relay.pin8, D22.A, D23.A, D24.A
  Level Switch -: Waste_Pump_Level_Switch_Relay.pin1, D1.C, Allen_Bradley_Micro_850.pin62, Allen_Bradley_Micro_850.pin63
  N2: Waste_Pump_Level_Switch_Relay.pin5, Allen_Bradley_Micro_850.pin5
  N3: Waste_Pump_Level_Switch_Relay.pin6, Man_Air_Valve_PLC_Relay.pin4
  N4: Man_Air_Valve_PLC_Relay.pin1, D2.C, Allen_Bradley_Micro_850.pin6
  N5: Man_Air_Valve_PLC_Relay.pin3, Pressure_Washer_PLC_Relay.pin1, D3.C, Allen_Bradley_Micro_850.pin56, Allen_Bradley_Micro_850.pin58
  N6: Man_Air_Valve_PLC_Relay.pin6, Main_Air_Valve_Relay.pin1, D16.C
  N7: Pressure_Washer_PLC_Relay.pin3, Main_Water_Valve_Relay.pin1, D15.C
  Pressure Washer Contactor +: Pressure_Washer_PLC_Relay.pin6
  PLC PSU C1 +24: Allen_Bradley_Micro_850.pin1
  PLC PSU C1 -24: Allen_Bradley_Micro_850.pin2
  N8: Allen_Bradley_Micro_850.pin7, Valve_1-1_Relay.pin1, D21.C
  N9: Allen_Bradley_Micro_850.pin10, Valve_1-2_Relay.pin1, D20.C
  N10: Allen_Bradley_Micro_850.pin11, Valve_1-3_Relay.pin1, D19.C
  N11: Allen_Bradley_Micro_850.pin12, Valve_1-4_Relay.pin1, D24.C
  N12: Allen_Bradley_Micro_850.pin13, Valve_2-1_Relay.pin1, D22.C
  N13: Allen_Bradley_Micro_850.pin14, Valve_2-2_Relay.pin1, D23.C
  N14: Allen_Bradley_Micro_850.pin15, Valve_2-3_Relay.pin1, D18.C
  N15: Allen_Bradley_Micro_850.pin18, Valve_2-4_Relay.pin1, D17.C
  Stop Light +: Allen_Bradley_Micro_850.pin19
  Pause Light +: Allen_Bradley_Micro_850.pin20
  Start Light +: Allen_Bradley_Micro_850.pin21
  Error Light +: Allen_Bradley_Micro_850.pin22
  Washing Indicator +: Allen_Bradley_Micro_850.pin23
  Drying Indicator +: Allen_Bradley_Micro_850.pin26
  Pumping Indicator +: Allen_Bradley_Micro_850.pin27
  Stop Button -: Allen_Bradley_Micro_850.pin59
  Pause Button -: Allen_Bradley_Micro_850.pin60
  Start Button -: Allen_Bradley_Micro_850.pin61
  AUX PSU C1 +24: Main_Air_Valve_Relay.pin2, Main_Air_Valve_Relay.pin5, Main_Water_Valve_Relay.pin2, Main_Water_Valve_Relay.pin5, Valve_1-3_Relay.pin2, Valve_1-3_Relay.pin5, Valve_1-2_Relay.pin2, Valve_1-2_Relay.pin5, Valve_1-1_Relay.pin2, Valve_1-1_Relay.pin5
  Air Valve p1: Main_Air_Valve_Relay.pin3
  AUX PSU C1 -24: Main_Air_Valve_Relay.pin4, Main_Air_Valve_Relay.pin7, Main_Water_Valve_Relay.pin4, Main_Water_Valve_Relay.pin7, Valve_1-3_Relay.pin4, Valve_1-3_Relay.pin7, Valve_1-2_Relay.pin4, Valve_1-2_Relay.pin7, Valve_1-1_Relay.pin4, Valve_1-1_Relay.pin7
  Air Valve p3: Main_Air_Valve_Relay.pin6
  N16: Main_Air_Valve_Relay.pin8, D16.A
  Water Valve p1: Main_Water_Valve_Relay.pin3
  Water Valve p3: Main_Water_Valve_Relay.pin6
  AUX PSU C2 +24: Valve_2-4_Relay.pin2, Valve_2-4_Relay.pin5, Valve_2-3_Relay.pin2, Valve_2-3_Relay.pin5, Valve_1-4_Relay.pin2, Valve_1-4_Relay.pin5, Valve_2-1_Relay.pin2, Valve_2-1_Relay.pin5, Valve_2-2_Relay.pin2, Valve_2-2_Relay.pin5
  Valve 2-4 p1: Valve_2-4_Relay.pin3
  AUX PSU C2 -24: Valve_2-4_Relay.pin4, Valve_2-4_Relay.pin7, Valve_2-3_Relay.pin4, Valve_2-3_Relay.pin7, Valve_1-4_Relay.pin4, Valve_1-4_Relay.pin7, Valve_2-1_Relay.pin4, Valve_2-1_Relay.pin7, Valve_2-2_Relay.pin4, Valve_2-2_Relay.pin7
  Valve 2-4 p3: Valve_2-4_Relay.pin6
  Valve 2-3 p1: Valve_2-3_Relay.pin3
  Valve 2-3 p3: Valve_2-3_Relay.pin6
  Valve 1-3 p1: Valve_1-3_Relay.pin3
  Valve 1-3 p3: Valve_1-3_Relay.pin6
  Valve 1-2 p1: Valve_1-2_Relay.pin3
  Valve 1-2 p3: Valve_1-2_Relay.pin6
  Valve 1-1 p1: Valve_1-1_Relay.pin3
  Valve 1-1 p3: Valve_1-1_Relay.pin6
  Valve 1-4 p1: Valve_1-4_Relay.pin3
  Valve 1-4 p3: Valve_1-4_Relay.pin6
  Valve 2-1 p1: Valve_2-1_Relay.pin3
  Valve 2-1 p3: Valve_2-1_Relay.pin6
  Valve 2-2 p1: Valve_2-2_Relay.pin3
  Valve 2-2 p3: Valve_2-2_Relay.pin6
