# Fritzing sketch PLC_Diag_3 (saved by Fritzing 0.9.3b)
breadboards: 1

parts:
  WP_PLC_RL = IC, DIP package, 8 pins [chip_label="DPDT Relay" part_number=52111]
  WP_LS_RL = IC, DIP package, 8 pins [chip_label="DPDT Relay" part_number=52111]
  MAV_PLC_RL = IC, DIP package, 8 pins [chip_label="DPDT Relay" part_number=52111]
  PW_PLC_RL = IC, DIP package, 8 pins [chip_label="DPDT Relay" part_number=52111]
  WP_LS_RP = Diode [package=diode-1n4148]
  MAV_PLC_RP = Diode [package=diode-1n4148]
  PW_PLC_RP = Diode [package=diode-1n4148]
  WP_PLC_RP = Diode [package=diode-1n4148]
  Allen_Bradley_Micro_850 = IC, DIP package, 64 pins [chip_label="Micro 850" part_number=2080-L50E-48QBB]
  MAV_RL = IC, DIP package, 8 pins [chip_label="DPDT Relay" part_number=52111]
  MWV_RL = IC, DIP package, 8 pins [chip_label="DPDT Relay" part_number=52111]
  MWV_RP = Diode [package=diode-1n4148]
  MAV_RP = Diode [package=diode-1n4148]
  V2-4_RL = IC, DIP package, 8 pins [chip_label="DPDT Relay" part_number=52111]
  V2-3_RL = IC, DIP package, 8 pins [chip_label="DPDT Relay" part_number=52111]
  V2-4_RP = Diode [package=diode-1n4148]
  V2-3_RP = Diode [package=diode-1n4148]
  V1-3_RL = IC, DIP package, 8 pins [chip_label="DPDT Relay" part_number=52111]
  V1-3_RP = Diode [package=diode-1n4148]
  V1-2_RL = IC, DIP package, 8 pins [chip_label="DPDT Relay" part_number=52111]
  V1-2_RP = Diode [package=diode-1n4148]
  V1-1_RL = IC, DIP package, 8 pins [chip_label="DPDT Relay" part_number=52111]
  V1-1_RP = Diode [package=diode-1n4148]
  V1-4_RL = IC, DIP package, 8 pins [chip_label="DPDT Relay" part_number=52111]
  V2-1_RL = IC, DIP package, 8 pins [chip_label="DPDT Relay" part_number=52111]
  V2-2_RL = IC, DIP package, 8 pins [chip_label="DPDT Relay" part_number=52111]
  V2-1_RP = Diode [package=diode-1n4148]
  V2-2_RP = Diode [package=diode-1n4148]
  V1-4_RP = Diode [package=diode-1n4148]

nets:
  N1: WP_PLC_RL.pin1, WP_PLC_RP.C, Allen_Bradley_Micro_850.pin4
  NC: WP_PLC_RL.pin2, WP_PLC_RL.pin3, WP_PLC_RL.pin4, WP_PLC_RL.pin5, WP_LS_RL.pin4
  Waste Pump Contactor +: WP_PLC_RL.pin6, WP_LS_RL.pin3
  Button Panel +/LS +/PLC PSU C2 +24: WP_PLC_RL.pin7, WP_LS_RL.pin2, MAV_PLC_RL.pin7, PW_PLC_RL.pin2, PW_PLC_RL.pin7, Allen_Bradley_Micro_850.pin3, Allen_Bradley_Micro_850.pin9, Allen_Bradley_Micro_850.pin17, Allen_Bradley_Micro_850.pin25
  Button Panel -/PLC PSU C2 -24/PW CT -/WP CT -: WP_PLC_RL.pin8, WP_LS_RL.pin7, WP_LS_RL.pin8, MAV_PLC_RL.pin2, MAV_PLC_RL.pin5, MAV_PLC_RL.pin8, PW_PLC_RL.pin4, PW_PLC_RL.pin5, PW_PLC_RL.pin8, WP_LS_RP.A, MAV_PLC_RP.A, PW_PLC_RP.A, WP_PLC_RP.A, Allen_Bradley_Micro_850.pin8, Allen_Bradley_Micro_850.pin16, Allen_Bradley_Micro_850.pin24, Allen_Bradley_Micro_850.pin30, Allen_Bradley_Micro_850.pin41, Allen_Bradley_Micro_850.pin50, Allen_Bradley_Micro_850.pin57, Allen_Bradley_Micro_850.pin64, MWV_RL.pin8, MWV_RP.A, V2-4_RL.pin8, V2-3_RL.pin8, V2-4_RP.A, V2-3_RP.A, V1-3_RL.pin8, V1-3_RP.A, V1-2_RL.pin8, V1-2_RP.A, V1-1_RL.pin8, V1-1_RP.A, V1-4_RL.pin8, V2-1_RL.pin8, V2-2_RL.pin8, V2-1_RP.A, V2-2_RP.A, V1-4_RP.A
  Level Switch -: WP_LS_RL.pin1, WP_LS_RP.C, Allen_Bradley_Micro_850.pin62, Allen_Bradley_Micro_850.pin63
  N2: WP_LS_RL.pin5, Allen_Bradley_Micro_850.pin5
  N3: WP_LS_RL.pin6, MAV_PLC_RL.pin4
  N4: MAV_PLC_RL.pin1, MAV_PLC_RP.C, Allen_Bradley_Micro_850.pin6
  N5: MAV_PLC_RL.pin3, PW_PLC_RL.pin1, PW_PLC_RP.C, Allen_Bradley_Micro_850.pin56, Allen_Bradley_Micro_850.pin58
  N6: MAV_PLC_RL.pin6, MAV_RL.pin1, MAV_RP.C
  N7: PW_PLC_RL.pin3, MWV_RL.pin1, MWV_RP.C
  Pressure Washer Contactor +: PW_PLC_RL.pin6
  PLC PSU C1 +24: Allen_Bradley_Micro_850.pin1
  PLC PSU C1 -24: Allen_Bradley_Micro_850.pin2
  N8: Allen_Bradley_Micro_850.pin7, V1-1_RL.pin1, V1-1_RP.C
  N9: Allen_Bradley_Micro_850.pin10, V1-2_RL.pin1, V1-2_RP.C
  N10: Allen_Bradley_Micro_850.pin11, V1-3_RL.pin1, V1-3_RP.C
  N11: Allen_Bradley_Micro_850.pin12, V1-4_RL.pin1, V1-4_RP.C
  N12: Allen_Bradley_Micro_850.pin13, V2-1_RL.pin1, V2-1_RP.C
  N13: Allen_Bradley_Micro_850.pin14, V2-2_RL.pin1, V2-2_RP.C
  N14: Allen_Bradley_Micro_850.pin15, V2-3_RL.pin1, V2-3_RP.C
  N15: Allen_Bradley_Micro_850.pin18, V2-4_RL.pin1, V2-4_RP.C
  Stop Light +: Allen_Bradley_Micro_850.pin19
  Pause Light +: Allen_Bradley_Micro_850.pin20
  Start Light +: Allen_Bradley_Micro_850.pin21
  Error Light +: Allen_Bradley_Micro_850.pin22
  Washing Indicator +: Allen_Bradley_Micro_850.pin23
  Drying Indicator +: Allen_Bradley_Micro_850.pin26
  Pumping Indicator +: Allen_Bradley_Micro_850.pin27
  Stop Button -: Allen_Bradley_Micro_850.pin59
  Pause Button -: Allen_Bradley_Micro_850.pin60
  Start Button -: Allen_Bradley_Micro_850.pin61
  AUX PSU C1 +24: MAV_RL.pin2, MAV_RL.pin5, MWV_RL.pin2, MWV_RL.pin5, V1-3_RL.pin2, V1-3_RL.pin5, V1-2_RL.pin2, V1-2_RL.pin5, V1-1_RL.pin2, V1-1_RL.pin5
  Air Valve p1: MAV_RL.pin3
  AUX PSU C1 -24: MAV_RL.pin4, MAV_RL.pin7, MWV_RL.pin4, MWV_RL.pin7, V1-3_RL.pin4, V1-3_RL.pin7, V1-2_RL.pin4, V1-2_RL.pin7, V1-1_RL.pin4, V1-1_RL.pin7
  Air Valve p3: MAV_RL.pin6
  N16: MAV_RL.pin8, MAV_RP.A
  Water Valve p1: MWV_RL.pin3
  Water Valve p3: MWV_RL.pin6
  AUX PSU C2 +24: V2-4_RL.pin2, V2-4_RL.pin5, V2-3_RL.pin2, V2-3_RL.pin5, V1-4_RL.pin2, V1-4_RL.pin5, V2-1_RL.pin2, V2-1_RL.pin5, V2-2_RL.pin2, V2-2_RL.pin5
  Valve 2-4 p1: V2-4_RL.pin3
  AUX PSU C2 -24: V2-4_RL.pin4, V2-4_RL.pin7, V2-3_RL.pin4, V2-3_RL.pin7, V1-4_RL.pin4, V1-4_RL.pin7, V2-1_RL.pin4, V2-1_RL.pin7, V2-2_RL.pin4, V2-2_RL.pin7
  Valve 2-4 p3: V2-4_RL.pin6
  Valve 2-3 p1: V2-3_RL.pin3
  Valve 2-3 p3: V2-3_RL.pin6
  Valve 1-3 p1: V1-3_RL.pin3
  Valve 1-3 p3: V1-3_RL.pin6
  Valve 1-2 p1: V1-2_RL.pin3
  Valve 1-2 p3: V1-2_RL.pin6
  Valve 1-1 p1: V1-1_RL.pin3
  Valve 1-1 p3: V1-1_RL.pin6
  Valve 1-4 p1: V1-4_RL.pin3
  Valve 1-4 p3: V1-4_RL.pin6
  Valve 2-1 p1: V2-1_RL.pin3
  Valve 2-1 p3: V2-1_RL.pin6
  Valve 2-2 p1: V2-2_RL.pin3
  Valve 2-2 p3: V2-2_RL.pin6
