# Fritzing sketch PLC_Diag_two_valve (saved by Fritzing 0.9.3b)
breadboards: 1

parts:
  WP_PLC_RL = IC, DIP package, 8 pins [chip_label="DPDT Relay" part_number=52111]
  WP_LS_RL = IC, DIP package, 8 pins [chip_label="DPDT Relay" part_number=52111]
  MAV_PLC_RL = IC, DIP package, 8 pins [chip_label="DPDT Relay" part_number=52111]
  PW_PLC_RL = IC, DIP package, 8 pins [chip_label="DPDT Relay" part_number=52111]
  WP_LS_RP = Diode [package=diode-1n4148]
  MAV_PLC_RP = Diode [package=diode-1n4148]
  PW_PLC_RP = Diode [package=diode-1n4148]
  WP_PLC_RP = Diode [package=diode-1n4148]
  Allen_Bradley_Micro_850 = IC, DIP package, 64 pins [chip_label="Micro 850" part_number=2080-L50E-48QBB]
  MWV_RL1 = IC, DIP package, 8 pins [chip_label="DPDT Relay" part_number=52111]
  MAV_RL1 = IC, DIP package, 8 pins [chip_label="DPDT Relay" part_number=52111]
  MAV_RP1 = Diode [package=diode-1n4148]
  MWV_RP1 = Diode [package=diode-1n4148]

nets:
  N1: WP_PLC_RL.pin1, WP_PLC_RP.C, Allen_Bradley_Micro_850.pin4
  NC: WP_PLC_RL.pin2, WP_PLC_RL.pin3, WP_PLC_RL.pin4, WP_PLC_RL.pin5, WP_LS_RL.pin4
  Waste Pump Contactor +: WP_PLC_RL.pin6, WP_LS_RL.pin3
  N2: WP_PLC_RL.pin7, WP_LS_RL.pin2
  AUX PSU C1 -24/AUX PSU C2 -24/Button Panel -/PW CT -/WP CT -: WP_PLC_RL.pin8, WP_LS_RL.pin7, WP_LS_RL.pin8, MAV_PLC_RL.pin2, MAV_PLC_RL.pin5, MAV_PLC_RL.pin8, PW_PLC_RL.pin4, PW_PLC_RL.pin5, PW_PLC_RL.pin8, WP_LS_RP.A, MAV_PLC_RP.A, PW_PLC_RP.A, WP_PLC_RP.A, Allen_Bradley_Micro_850.pin8, Allen_Bradley_Micro_850.pin64, MWV_RL1.pin4, MAV_RL1.pin4
  Level Switch -: WP_LS_RL.pin1, WP_LS_RP.C, Allen_Bradley_Micro_850.pin62, Allen_Bradley_Micro_850.pin63
  N3: WP_LS_RL.pin5, Allen_Bradley_Micro_850.pin5
  N4: WP_LS_RL.pin6, MAV_PLC_RL.pin4
  N5: MAV_PLC_RL.pin1, MAV_PLC_RP.C, Allen_Bradley_Micro_850.pin6
  N6: MAV_PLC_RL.pin3, PW_PLC_RL.pin1, PW_PLC_RP.C
  N7: MAV_PLC_RL.pin6, MAV_RL1.pin1, MWV_RP1.C
  AUX PSU C1 +24/AUX PSU C2 +24/Button Panel +/LS +: MAV_PLC_RL.pin7, PW_PLC_RL.pin2, PW_PLC_RL.pin7, Allen_Bradley_Micro_850.pin3, Allen_Bradley_Micro_850.pin9, MWV_RL1.pin2, MWV_RL1.pin5, MAV_RL1.pin2, MAV_RL1.pin5
  N8: PW_PLC_RL.pin3, MWV_RL1.pin1, MAV_RP1.C
  Pressure Washer Contactor +: PW_PLC_RL.pin6
  PLC PSU C1 +24: Allen_Bradley_Micro_850.pin1
  PLC PSU C1 -24: Allen_Bradley_Micro_850.pin2
  Stop Light +: Allen_Bradley_Micro_850.pin7
  Pause Light +: Allen_Bradley_Micro_850.pin10
  Start Light +: Allen_Bradley_Micro_850.pin11
  Stop Button -: Allen_Bradley_Micro_850.pin59
  Pause Button -: Allen_Bradley_Micro_850.pin60
  Start Button -: Allen_Bradley_Micro_850.pin61
  Water Valve p1: MWV_RL1.pin3
  Water Valve p3: MWV_RL1.pin6
  N9: MWV_RL1.pin7, MWV_RL1.pin8, MAV_RP1.A
  Air Valve p1: MAV_RL1.pin3
  Air Valve p3: MAV_RL1.pin6
  N10: MAV_RL1.pin7, MAV_RL1.pin8, MWV_RP1.A
