# Fritzing sketch Term_Blocks (saved by Fritzing 0.9.3b)
breadboards: 1

parts:
  WP_PLC_RL1 = IC, DIP package, 8 pins [chip_label="DPDT Relay" part_number=52111]
  WP_LS_RL2 = IC, DIP package, 8 pins [chip_label="DPDT Relay" part_number=52111]
  MAV_PLC_RL3 = IC, DIP package, 8 pins [chip_label="DPDT Relay" part_number=52111]
  PW_RL4 = IC, DIP package, 8 pins [chip_label="DPDT Relay" part_number=52111]
  Allen_Bradley_Micro_850 = IC, DIP package, 64 pins [chip_label="Micro 850" part_number=2080-L50E-48QBB]
  MWV_RL5 = IC, DIP package, 8 pins [chip_label="DPDT Relay" part_number=52111]
  MAV_RL6 = IC, DIP package, 8 pins [chip_label="DPDT Relay" part_number=52111]
  TB1 = Camdenboss CTB0158-3 [part_number=3PTB package=THT]
  TB3 = Camdenboss CTB0158-3 [part_number=3PTB package=THT]
  TB2 = Camdenboss CTB0158-4 [part_number=4PTB package=THT]
  TB4 = Camdenboss CTB0158-3 [part_number=3PTB package=THT]
  TB6 = Camdenboss CTB0158-3 [part_number=3PTB package=THT]
  Washer_Connector = Camdenboss CTB0158-6 [part_number=CTB0158-6 package=THT]
  Washer_Connector1 = Camdenboss CTB0158-12 [part_number=CTB0158-12 package=THT]
  Washer_Connector2 = Camdenboss CTB0158-8 [part_number=CTB0158-8 package=THT]
  Washer_Connector3 = Camdenboss CTB0158-8 [part_number=CTB0158-8 package=THT]
  TB5 = Camdenboss CTB0158-4 [part_number=4PTB package=THT]
  J6 = Camdenboss CTB0158-2 [part_number=2PTB package=THT]  # not connected
  J7 = Camdenboss CTB0158-2 [part_number=2PTB package=THT]
  J8 = Camdenboss CTB0158-2 [part_number=2PTB package=THT]
  Electrical_Connector = Camdenboss CTB0158-10 [part_number=CTB0158-10 package=THT]
  J9 = Camdenboss CTB0158-2 [part_number=2PTB package=THT]
  Front_Panel_Connector = Camdenboss CTB0158-8 [part_number=CTB0158-8 package=THT]
  RP = IC, DIP package, 12 pins [chip_label=Transorb]

nets:
  N1: WP_PLC_RL1.pin1, TB1.pin3
  NC: WP_PLC_RL1.pin2, WP_PLC_RL1.pin3, WP_PLC_RL1.pin4, WP_PLC_RL1.pin5, WP_LS_RL2.pin4, MWV_RL5.pin3, MWV_RL5.pin6, MAV_RL6.pin6, Washer_Connector.pin3, Washer_Connector.pin4
  N2: WP_PLC_RL1.pin6, WP_LS_RL2.pin3, Electrical_Connector.terminal_7
  N3: WP_PLC_RL1.pin7, WP_LS_RL2.pin2, Washer_Connector3.terminal_3
  N4: WP_PLC_RL1.pin8, Washer_Connector1.terminal_9
  N5: WP_LS_RL2.pin1, TB2.pin4
  N6: WP_LS_RL2.pin5, Allen_Bradley_Micro_850.pin5
  N7: WP_LS_RL2.pin6, MAV_PLC_RL3.pin4
  N8: WP_LS_RL2.pin7, WP_LS_RL2.pin8, Washer_Connector1.terminal_10
  N9: MAV_PLC_RL3.pin1, TB3.pin3
  N10: MAV_PLC_RL3.pin2, Washer_Connector1.terminal_11
  N11: MAV_PLC_RL3.pin3, TB4.pin2
  N12: MAV_PLC_RL3.pin5, MAV_PLC_RL3.pin8, Washer_Connector1.terminal_12
  N13: MAV_PLC_RL3.pin6, TB6.pin2
  N14: MAV_PLC_RL3.pin7, PW_RL4.pin2, Washer_Connector3.terminal_4
  N15: PW_RL4.pin1, TB4.pin3
  N16: PW_RL4.pin3, TB5.pin2
  N17: PW_RL4.pin4, Washer_Connector2.terminal_1
  N18: PW_RL4.pin5, PW_RL4.pin8, Washer_Connector2.terminal_2
  N19: PW_RL4.pin6, Electrical_Connector.terminal_9
  N20: PW_RL4.pin7, MWV_RL5.pin2, Washer_Connector3.terminal_5
  N21: Allen_Bradley_Micro_850.pin1, Electrical_Connector.terminal_1
  N22: Allen_Bradley_Micro_850.pin2, Electrical_Connector.terminal_2
  N23: Allen_Bradley_Micro_850.pin3, Allen_Bradley_Micro_850.pin9, Washer_Connector3.terminal_8
  N24: Allen_Bradley_Micro_850.pin4, TB1.terminal_2
  N25: Allen_Bradley_Micro_850.pin6, TB3.terminal_2
  N26: Allen_Bradley_Micro_850.pin7, Front_Panel_Connector.terminal_6
  N27: Allen_Bradley_Micro_850.pin8, Allen_Bradley_Micro_850.pin16, Washer_Connector1.terminal_2
  N28: Allen_Bradley_Micro_850.pin10, Front_Panel_Connector.terminal_5
  N29: Allen_Bradley_Micro_850.pin11, Front_Panel_Connector.terminal_4
  N30: Allen_Bradley_Micro_850.pin56, Allen_Bradley_Micro_850.pin58, TB5.terminal_4
  N31: Allen_Bradley_Micro_850.pin59, Front_Panel_Connector.terminal_1
  N32: Allen_Bradley_Micro_850.pin60, Front_Panel_Connector.terminal_2
  N33: Allen_Bradley_Micro_850.pin61, Front_Panel_Connector.terminal_3
  N34: Allen_Bradley_Micro_850.pin62, Allen_Bradley_Micro_850.pin63, TB2.terminal_3
  N35: Allen_Bradley_Micro_850.pin64, Washer_Connector1.terminal_1
  N36: MWV_RL5.pin1, TB5.pin3
  N37: MWV_RL5.pin4, Washer_Connector2.terminal_3
  N38: MWV_RL5.pin5, MAV_RL6.pin2, Washer_Connector3.terminal_6
  N39: MWV_RL5.pin7, MWV_RL5.pin8, Washer_Connector2.terminal_4
  N40: MAV_RL6.pin1, TB6.pin3
  N41: MAV_RL6.pin3, Washer_Connector.terminal_2
  N42: MAV_RL6.pin4, Washer_Connector2.terminal_5
  N43: MAV_RL6.pin5, Washer_Connector3.terminal_7
  N44: MAV_RL6.pin7, MAV_RL6.pin8, Washer_Connector.terminal_1, Washer_Connector2.terminal_6
  N45: TB1.pin1, RP.pin12
  N46: TB3.pin1, RP.pin10
  N47: TB2.pin1, RP.pin11
  N48: TB2.pin2, Washer_Connector.terminal_6
  N49: TB4.pin1, RP.pin9
  N50: TB6.pin1, RP.pin7
  Air Valve -: Washer_Connector.pin1
  Air Valve +: Washer_Connector.pin2
  Level Switch +: Washer_Connector.pin5
  Level Switch -: Washer_Connector.pin6
  N51: Washer_Connector.terminal_5, J7.terminal_1
  N52: Washer_Connector1.terminal_3, RP.pin1
  N53: Washer_Connector1.terminal_4, RP.pin2
  N54: Washer_Connector1.terminal_5, RP.pin3
  N55: Washer_Connector1.terminal_6, RP.pin4
  N56: Washer_Connector1.terminal_7, RP.pin5
  N57: Washer_Connector1.terminal_8, RP.pin6
  N58: Washer_Connector2.terminal_7, Front_Panel_Connector.terminal_7
  N59: Washer_Connector3.pin1, Electrical_Connector.terminal_5
  N60: Washer_Connector3.pin2, Electrical_Connector.terminal_6
  N61: TB5.pin1, RP.pin8
  N62: J7.terminal_2, Front_Panel_Connector.terminal_8
  N63: J8.pin1, Electrical_Connector.terminal_3
  N64: J8.pin2, Electrical_Connector.terminal_4
  PLC PSU C1 +24: Electrical_Connector.pin1
  PLC PSU C1 -24: Electrical_Connector.pin2
  AUX PSU C1-: Electrical_Connector.pin3
  AUX PSU C2-: Electrical_Connector.pin4
  AUX PSU C2+: Electrical_Connector.pin5
  AUX PSU C1+: Electrical_Connector.pin6
  Waste Pump Contactor +: Electrical_Connector.pin7
  Waste Pump Contactor -: Electrical_Connector.pin8
  Pressure Washer Contactor +: Electrical_Connector.pin9
  Pressure Washer Contactor -: Electrical_Connector.pin10
  N65: Electrical_Connector.terminal_8, J9.pin1
  N66: Electrical_Connector.terminal_10, J9.pin2
  Stop Button -: Front_Panel_Connector.pin1
  Pause Button -: Front_Panel_Connector.pin2
  Start Button -: Front_Panel_Connector.pin3
  Start Light +: Front_Panel_Connector.pin4
  Pause Light +: Front_Panel_Connector.pin5
  Stop Light +: Front_Panel_Connector.pin6
  Button Panel -: Front_Panel_Connector.pin7
  Button Panel +: Front_Panel_Connector.pin8
