// Logisim project Relay_Test.circ as structural Verilog: 10 circuits, main circuit main
module DPDT_Relay (
  input  In1_1,
  input  In1_2,
  input  Switch_PLUS,
  input  In2_1,
  input  Switch_MINUS,
  input  In2_2,
  output Out1,
  output Out2
);

  wire multiplexer_1_out, not_1_out, not_2_out;

  Multiplexer multiplexer_1 (.in0(Switch_PLUS), .in1(1'b0), .out(multiplexer_1_out), .sel(Switch_MINUS));
  Pull_Resistor pull_resistor_1 (.node(multiplexer_1_out));
  not not_1 (not_1_out, multiplexer_1_out);
  not not_2 (not_2_out, multiplexer_1_out);
  // Transmission_Gate transmission_1: pin names not known; wires that end beside it: In1_1, multiplexer_1_out, not_1_out, Out1
  // Transmission_Gate transmission_2: pin names not known; wires that end beside it: In1_2, not_1_out, multiplexer_1_out, Out1
  // Transmission_Gate transmission_3: pin names not known; wires that end beside it: In2_1, multiplexer_1_out, not_2_out, Out2
  // Transmission_Gate transmission_4: pin names not known; wires that end beside it: In2_2, not_2_out, multiplexer_1_out, Out2
endmodule

module main (
  input  Waste_Pump_PLC_Out,
  input  Air_PLC_Out,
  input  Water_PLC_Out,
  output Waste_Level_PLC_In,
  output Water_Relay_State_PLC_In,
  output Waste_Pump_Power,
  output Air_Solenoid,
  output Pressure_Washer_Power
);

  wire dpdt_relay_1_out2, source_1_o, source_2_o, source_3_o;

  Source source_1 (.CTRL(Waste_Pump_PLC_Out), .O(source_1_o));
  Source source_2 (.CTRL(Air_PLC_Out), .O(source_2_o));
  Source source_3 (.CTRL(Water_PLC_Out), .O(source_3_o));
  // Switch Waste_Level: pin names not known; wires that end beside it: 1'b1, Waste_Level_PLC_In
  SPST_Relay spst_relay_1 (.Switch_Plus(source_1_o), .Switch_Minus(1'b0), .I(1'b1), .O(Waste_Pump_Power));
  DPDT_Relay dpdt_relay_1 (
    .Switch_PLUS(Waste_Level_PLC_In), .Switch_MINUS(1'b0), .In1_2(1'b1), .In2_1(source_3_o), .In2_2(1'b0),
    .Out1(Waste_Pump_Power), .Out2(dpdt_relay_1_out2));  // open: In1_1
  Pull_Resistor pull_resistor_1 (.node(Waste_Pump_Power));
  DPDT_Relay dpdt_relay_2 (
    .Switch_PLUS(source_2_o), .Switch_MINUS(1'b0), .In1_1(1'b0), .In1_2(1'b1), .In2_1(dpdt_relay_1_out2),
    .In2_2(1'b0), .Out1(Air_Solenoid), .Out2(Water_Relay_State_PLC_In));
  DPDT_Relay dpdt_relay_3 (
    .Switch_PLUS(Water_Relay_State_PLC_In), .Switch_MINUS(1'b0), .In1_1(1'b0), .In1_2(1'b1), .In2_1(1'b0),
    .In2_2(1'b1), .Out1(Pressure_Washer_Power));  // open: Out2
  Pull_Resistor pull_resistor_2 (.node(Water_Relay_State_PLC_In));
  Pull_Resistor pull_resistor_3 (.node(Waste_Level_PLC_In));

  // Notes on the sheet:
  //   120VAC
  //   24VDC
endmodule

module TPTT_Relay (
  input  In1_1,
  input  Switch,
  input  In1_2,
  input  In2_1,
  input  In2_2,
  input  In3_1,
  input  In3_3,
  output Out1,
  output Out2,
  output Out3
);

  wire not_1_out, not_2_out, not_3_out;

  not not_1 (not_1_out, Switch);
  not not_2 (not_2_out, Switch);
  not not_3 (not_3_out, Switch);
  // Transmission_Gate transmission_1: pin names not known; wires that end beside it: In1_1, Switch, not_1_out, Out1
  // Transmission_Gate transmission_2: pin names not known; wires that end beside it: In1_2, not_1_out, Switch, Out1
  // Transmission_Gate transmission_3: pin names not known; wires that end beside it: In2_1, Switch, not_2_out, Out2
  // Transmission_Gate transmission_4: pin names not known; wires that end beside it: In2_2, not_2_out, Switch, Out2
  // Transmission_Gate transmission_5: pin names not known; wires that end beside it: In3_1, Switch, not_3_out, Out3
  // Transmission_Gate transmission_6: pin names not known; wires that end beside it: In3_3, not_3_out, Switch, Out3
endmodule

module SPST_Relay (
  input  I,
  input  Switch_Plus,
  input  Switch_Minus,
  output O
);

  wire not_1_out, pull_resistor_1_node;

  Pull_Resistor pull_resistor_1 (.node(pull_resistor_1_node));
  Multiplexer multiplexer_1 (.in0(Switch_Plus), .in1(1'b0), .out(pull_resistor_1_node), .sel(Switch_Minus));
  not not_1 (not_1_out, pull_resistor_1_node);
  // Transmission_Gate transmission_1: pin names not known; wires that end beside it: I, not_1_out, pull_resistor_1_node, O
endmodule

module Main_2 (
  input  Air_PLC_Out,
  input  Waste_Pump_PLC_Out,
  input  Water_PLC_Out,
  output Waste_Level_PLC_In,
  output Water_Relay_State_PLC_In,
  output Waste_Pump_Power,
  output Air_Solenoid,
  output Pressure_Washer_Power,
  output Main_Water_Solenoid
);

  wire dpdt_relay_1_out2, source_1_o, source_2_o, source_3_o;

  // Switch Waste_Level: pin names not known; wires that end beside it: 1'b1, Waste_Level_PLC_In
  Source source_1 (.CTRL(Air_PLC_Out), .O(source_1_o));
  Source source_2 (.CTRL(Waste_Pump_PLC_Out), .O(source_2_o));
  Source source_3 (.CTRL(Water_PLC_Out), .O(source_3_o));
  SPST_Relay spst_relay_1 (.Switch_Plus(source_2_o), .Switch_Minus(1'b0), .I(1'b1), .O(Waste_Pump_Power));
  DPDT_Relay dpdt_relay_1 (
    .Switch_PLUS(Waste_Level_PLC_In), .Switch_MINUS(1'b0), .In1_2(1'b1), .In2_1(source_3_o), .In2_2(1'b0),
    .Out1(Waste_Pump_Power), .Out2(dpdt_relay_1_out2));  // open: In1_1
  Pull_Resistor pull_resistor_1 (.node(Waste_Pump_Power));
  DPDT_Relay dpdt_relay_2 (
    .Switch_PLUS(source_1_o), .Switch_MINUS(1'b0), .In1_1(1'b0), .In1_2(1'b1), .In2_1(dpdt_relay_1_out2),
    .In2_2(1'b0), .Out1(Air_Solenoid), .Out2(Water_Relay_State_PLC_In));
  DPDT_Relay dpdt_relay_3 (
    .Switch_PLUS(Water_Relay_State_PLC_In), .Switch_MINUS(1'b0), .In1_1(1'b0), .In1_2(1'b1), .In2_1(1'b0),
    .In2_2(1'b1), .Out1(Pressure_Washer_Power), .Out2(Main_Water_Solenoid));
  Pull_Resistor pull_resistor_2 (.node(Waste_Level_PLC_In));
  Pull_Resistor pull_resistor_3 (.node(Water_Relay_State_PLC_In));

  // Notes on the sheet:
  //   24VDC
  //   120VAC FOR WASTE PUMP
  //   24VDC
  //   120VAC FOR PRESSURE WASHER
  //   24VDC
endmodule

module Sink (
  input  CTRL,
  output O
);

  wire undriven;

  Multiplexer multiplexer_1 (.in0(undriven), .in1(1'b0), .out(O), .sel(CTRL));
endmodule

module Source (
  input  CTRL,
  output O
);

  wire undriven;

  Multiplexer multiplexer_1 (.in0(undriven), .in1(1'b1), .out(O), .sel(CTRL));
endmodule

module Main3 (
  input  Waste_Pump_PLC_Out,
  input  Air_PLC_Out,
  input  Water_PLC_Out,
  output Waste_LV_To_PLC,
  output Water_Relay_State_To_PLC,
  output Waste_Pump_Power,
  output Air_Solenoid,
  output Pressure_Washer_Power,
  output Water_Solenoid
);

  wire dpdt_relay_1_out2, dpdt_relay_2_out2, pull_resistor_2_node, pull_resistor_3_node, source_1_o,
       source_2_o, source_3_o, Waste_Level_p2;

  Source source_1 (.CTRL(Waste_Pump_PLC_Out), .O(source_1_o));
  Source source_2 (.CTRL(Air_PLC_Out), .O(source_2_o));
  Source source_3 (.CTRL(Water_PLC_Out), .O(source_3_o));
  // Switch Waste_Level: pin names not known; wires that end beside it: 1'b0, Waste_Level_p2, 1'b1
  DPDT_Relay dpdt_relay_1 (
    .Switch_PLUS(source_1_o), .Switch_MINUS(1'b0), .In1_1(1'b0), .In1_2(1'b1), .In2_1(source_3_o),
    .In2_2(1'b0), .Out1(Waste_Pump_Power), .Out2(dpdt_relay_1_out2));
  DPDT_Relay dpdt_relay_2 (
    .Switch_PLUS(source_2_o), .Switch_MINUS(1'b0), .In1_1(1'b0), .In1_2(1'b1), .In2_1(dpdt_relay_1_out2),
    .In2_2(1'b0), .Out1(Air_Solenoid), .Out2(dpdt_relay_2_out2));
  Pull_Resistor #(.pull(1)) pull_resistor_1 ();  // open: node
  DPDT_Relay dpdt_relay_3 (
    .Switch_PLUS(dpdt_relay_2_out2), .Switch_MINUS(1'b0), .In1_1(1'b0), .In1_2(1'b1), .In2_1(1'b0),
    .In2_2(1'b1), .Out1(Pressure_Washer_Power), .Out2(Water_Solenoid));
  Pull_Resistor #(.pull(1)) pull_resistor_2 (.node(pull_resistor_2_node));
  Pull_Up_Output pull_up_output_1 (.Pull(pull_resistor_2_node), .I(Waste_Level_p2), .O(Waste_LV_To_PLC));
  Pull_Down_Output pull_down_output_1 (
    .Pull(pull_resistor_3_node), .I(dpdt_relay_2_out2), .O(Water_Relay_State_To_PLC));
  Pull_Resistor pull_resistor_3 (.node(pull_resistor_3_node));

  // Notes on the sheet:
  //   Waste_LV_To_PLC: pull=up
  //   120VAC
  //   24VDC
endmodule

module Pull_Up_Output (
  input  Pull,
  input  I,
  output O
);

  Pull_Resistor #(.pull(1)) pull_resistor_1 (.node(I));

  assign O = I;
endmodule

module Pull_Down_Output (
  input  Pull,
  input  I,
  output O
);

  Pull_Resistor pull_resistor_1 (.node(I));

  assign O = I;
endmodule
